# Fritzing sketch Encoder Head (saved by Fritzing 0.9.3b)

parts:
  Q1 = QRD1114 [part_number=QRF1114 package=qrd1114]
  J1 = female pin header, 3 pins [form="♀ (female)"]
  R1 = Resistor [tolerance=±5% resistance=220 package=THT]
  R2 = Resistor [tolerance=±5% resistance=10k package=THT]

nets:
  N1: Q1.E, J1.pin3, R2.Pin_0
  N2: Q1.C, Q1.K, J1.pin1
  N3: Q1.A, R1.Pin_0
  N4: J1.pin2, R1.Pin_1, R2.Pin_1

notes:
  GND
  5V
  OUT
